# Fritzing sketch Main Diagram (saved by Fritzing 0.9.9b)

parts:
  L298N1 = L298N DC motor driver
  M4 = DC Motor  # not connected
  VCC1 = Battery  # not connected
  Raspberry_Pi_1 = Raspberry Pi 3 [part_number=RPI-3-V1.2]
  M2 = DC Motor  # not connected

nets:
  GND: L298N1.GND, Raspberry_Pi_1.GND
  N1: L298N1.ENA, Raspberry_Pi_1.GIPO6
  N2: L298N1.ENB, Raspberry_Pi_1.GIPO26
  N3: L298N1.IN1, Raspberry_Pi_1.GIPO13
  N4: L298N1.IN2, Raspberry_Pi_1.GIPO12
  N5: L298N1.IN3, Raspberry_Pi_1.GIPO21
  N6: L298N1.IN4, Raspberry_Pi_1.GIPO20

notes:
  GND

custom parts:
  L298N DC motor driver: 2x DC motor driver with 78M05 positive voltage regulator (7..35 V) L298N: max 46 V, 2 A Set 5 V Enable jumper to enable 5 V regultor (needed for the L298N) and +5 V output at screw terminal or supply external +5 V at screw terminal Set ENA and/or ENB to +5 V to enable motor permanently or supply ENA and/or ENB with PWM signal IN1 and IN2 set rotation directory for motor A (OUT1/OUT2) IN2 and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
